# Fritzing sketch Sch_ESP32_CCS811 (saved by Fritzing 0.9.4)

parts:
  part = ESP32-38PinWide [part_number=ESP32-38PinWide]
  CCS811_-_CO2_&_TVOC = Adafruit CCS811

nets:
  N1: part.3.3, CCS811_-_CO2_&_TVOC.3.3V
  N2: part.GPIO21, CCS811_-_CO2_&_TVOC.SDA
  N3: part.GPIO22, CCS811_-_CO2_&_TVOC.SCL
  GND: part.GND, CCS811_-_CO2_&_TVOC.GND, CCS811_-_CO2_&_TVOC.!WAKE

custom parts:
  ESP32-38PinWide: Generic 38-Pin ESP32 with wide format (only access to one side of pins on a breadboard) based on Stephen Lilley's HiLetgo ESP-WROOM-32 ESP32 ESP-32S Development Board.
